// Logisim project tpfinal.circ as structural Verilog: 1 circuit, main circuit main
module main (
  input  clock,
  input  reset,
  input  disco,
  input  play,
  input  pause,
  input  stop,
  input  eject,
  output reproductor,
  output motor,
  output bandeja
);

  wire and_1_out, and_2_out, and_3_out, and_4_out, and_5_out, Counting, j_k_ff_1_q, j_k_ff_2_q, j_k_ff_6_q,
       j_k_ff_7_q, j_k_ff_8_q, not_1_out, not_2_out, not_3_out, not_4_out, NotCounting, or_1_out, or_2_out;

  not not_1 (not_1_out, bandeja);
  and and_1 (and_1_out, not_1_out, Counting);
  and and_2 (and_2_out, NotCounting, disco, play);
  or or_1 (or_1_out, stop, eject);
  not not_2 (not_2_out, j_k_ff_1_q);
  J_K_Flip_Flop j_k_ff_1 (
    .J(1'b1), .clk(clock), .K(1'b1), .Q(j_k_ff_1_q), .en(and_1_out), .reset(NotCounting));  // open: Qn, preset
  or or_2 (or_2_out, pause, or_1_out);
  J_K_Flip_Flop j_k_ff_2 (
    .J(j_k_ff_1_q), .clk(clock), .K(j_k_ff_1_q), .Q(j_k_ff_2_q), .en(and_1_out), .reset(NotCounting));  // open: Qn, preset
  not not_3 (not_3_out, j_k_ff_2_q);
  and and_3 (and_3_out, j_k_ff_1_q, j_k_ff_2_q);
  J_K_Flip_Flop j_k_ff_3 (
    .J(and_2_out), .clk(clock), .K(or_2_out), .Q(reproductor), .en(1'b1), .reset(reset));  // open: Qn, preset
  J_K_Flip_Flop j_k_ff_4 (
    .J(and_2_out), .clk(clock), .K(or_1_out), .Q(motor), .en(1'b1), .reset(reset));  // open: Qn, preset
  J_K_Flip_Flop j_k_ff_5 (
    .J(1'b1), .clk(eject), .K(1'b1), .Q(Counting), .Qn(NotCounting), .en(1'b1), .reset(reset));  // open: preset
  not not_4 (not_4_out, j_k_ff_6_q);
  J_K_Flip_Flop j_k_ff_6 (
    .J(and_3_out), .clk(clock), .K(and_3_out), .Q(j_k_ff_6_q), .en(and_1_out), .reset(NotCounting));  // open: Qn, preset
  and and_4 (and_4_out, and_3_out, j_k_ff_6_q);
  and and_5 (and_5_out, and_4_out, j_k_ff_7_q);
  J_K_Flip_Flop j_k_ff_7 (
    .J(and_4_out), .clk(clock), .K(and_4_out), .Q(j_k_ff_7_q), .en(and_1_out), .reset(NotCounting));  // open: Qn, preset
  J_K_Flip_Flop j_k_ff_8 (
    .J(and_5_out), .clk(clock), .K(and_5_out), .Q(j_k_ff_8_q), .en(and_1_out), .reset(NotCounting));  // open: Qn, preset
  and and_6 (bandeja, not_2_out, not_3_out, not_4_out, j_k_ff_7_q, j_k_ff_8_q);

  // Other names for the same wires on the sheet: CLK = clock; Tray = bandeja
endmodule
